// Logisim project 4-bit-cpu-v2.circ as structural Verilog: 2 circuits, main circuit main
module main (
  input  in_1,
  input  in_2,
  input  in_3,
  input  in_4,
  input  R_W_RAM,
  input  LDPC,
  input  RESET
);

  wire clock_1_out, counter_2_carry, decoder_1_out0, decoder_1_out1, decoder_1_out2, decoder_1_out3,
       decoder_2_out0, decoder_2_out1, decoder_2_out2, decoder_2_out3, not_1_out, not_2_out, RAMADDRR, ZE;
  wire [1:0] counter_2_q;
  wire [3:0] BUS_MUX, counter_1_q, multiplexer_1_out, ram_1_data, register_1_q, register_2_q, register_3_q,
       rom_1_data;

  not not_1 (not_1_out, LDPC);
  Clock clock_1 (.out(clock_1_out));
  Counter #(.width(4), .max('hf)) counter_1 (
    .load(LDPC), .D(multiplexer_1_out), .count(not_1_out), .Q(counter_1_q), .clk(clock_1_out), .clr(RESET));  // open: carry
  Register #(.width(4)) register_1 (
    .D(multiplexer_1_out), .en(RAMADDRR), .Q(register_1_q), .clk(clock_1_out));  // open: clr
  // Probe on RAMADDRR
  RAM #(.addrWidth(4), .dataWidth(4)) ram_1 (
    .addr(register_1_q), .data(ram_1_data), .clk(clock_1_out), .ld(not_2_out));  // open: sel, clr
  not not_2 (not_2_out, R_W_RAM);
  ROM #(.addrWidth(4), .dataWidth(4)) rom_1 (.addr(counter_1_q), .data(rom_1_data));  // open: sel
  assign ram_1_data = R_W_RAM ? multiplexer_1_out : 4'bz;  // Controlled_Buffer controlled_buffer_1
  Register #(.width(4)) register_2 (.D(multiplexer_1_out), .en(ZE), .Q(register_2_q), .clk(clock_1_out));  // open: clr
  // Probe on ZE
  Register #(.width(4)) register_3 (
    .D(rom_1_data), .en(counter_2_carry), .Q(register_3_q), .clk(clock_1_out));  // open: clr
  Multiplexer #(.select(2), .width(4)) multiplexer_1 (
    .in0(rom_1_data), .in1(ram_1_data), .in2(register_2_q), .out(multiplexer_1_out), .sel(BUS_MUX[1:0]),
    .en(1'b1));  // open: in3
  Decoder #(.select(4)) decoder_1 (
    .out0(decoder_1_out0), .out1(decoder_1_out1), .out2(decoder_1_out2), .out3(decoder_1_out3),
    .sel(register_3_q));  // open: out4, out5, out6, out7, out8, out9, out10, out11, out12, out13, out14, out15, en
  Counter #(.width(2), .max('h3)) counter_2 (
    .Q(counter_2_q), .carry(counter_2_carry), .clk(clock_1_out));  // open: load, D, count, clr
  Decoder #(.select(2)) decoder_2 (
    .out0(decoder_2_out0), .out1(decoder_2_out1), .out2(decoder_2_out2), .out3(decoder_2_out3),
    .sel(counter_2_q));  // open: en
  // OR_Gate or_1 has open pins: out=BUS_MUX[1]
  // OR_Gate or_2 has open pins: out=BUS_MUX[0]
  // OR_Gate or_3 has open pins: out=BUS_MUX[2]
  // OR_Gate or_4 has open pins: out=BUS_MUX[3]
  // Pins of 2 and 4 bits meet at BUS_MUX

  // Notes on the sheet:
  //   RAM
  //   PROG MEM
  //   contents of rom_1 (hex, n*v repeats v):
  //   1 2 3 4 5 6 7 1 9 a b c d e f
  //   Z REG
  //   INSTRUCTION REG
endmodule

module MOVZ (
  input  in_1
);

  // Probe on nothing
  // Probe on nothing
  // Probe on nothing
  // Probe on nothing
  // Probe on nothing
  // Probe on nothing
  // Probe on nothing
  // Probe on nothing

  // Notes on the sheet:
  //   LDPC
  //   R/W RAM
  //   ZE
  //   BMX0
  //   BMX1
  //   BRK
  //   RADDRE
endmodule
